# Fritzing sketch Схема БК (saved by Fritzing 0.9.5d)

parts:
  Вправо = Momentary Switch [package=ksa_sealed_tac_switch]
  Вниз = Momentary Switch [package=ksa_sealed_tac_switch]
  Влево = Momentary Switch [package=ksa_sealed_tac_switch]
  Вверх = Momentary Switch [package=ksa_sealed_tac_switch]
  R12 = Photocell (LDR) [package=THT]
  R13 = Resistor [tolerance=±5% power=0.25 resistance=47k package=THT]
  C1 = Electrolytic Capacitor [capacitance=10µF voltage=16V package="100 mil [THT, electrolytic]"]
  Part1 = Arduino Nano (Rev3.0)
  R14 = Resistor [tolerance=±5% resistance=1k package=THT]
  U1 = TMP01 - Low Power, Programmable Temperature Controller [part_number=TMP01]
  D1 = Rectifier Diode [part_number=1N4001 package="300 mil [THT]"]

nets:
  GND: Вправо.1, Вправо.2, Вниз.1, Вниз.2, Влево.1, Влево.2, Вверх.1, Вверх.2, R13.Pin_1, C1.-, Part1.GND, U1.GND
  N1: Вправо.3, Вправо.4, Part1.A0
  N2: Вниз.3, Вниз.4, Part1.A1
  N3: Влево.3, Влево.4, Part1.A2
  N4: Вверх.3, Вверх.4, Part1.A3
  +5В -: R12.pin_0
  N5: R12.pin_1, R13.Pin_0, C1.+, Part1.A7
  N6: Part1.D1/TX, U1.TX
  N7: Part1.D0/RX, U1.RX
  Сигнал расхода топлива .: Part1.D2
  5V: Part1.5V, U1.VCC
  K-Line .: R14.Pin_0, U1.K
  N8: R14.Pin_1, U1.VS, D1.cathode
  +12В .: D1.anode
